# Fritzing sketch L02_helloLED (saved by Fritzing 0.9.3b)
circuit board: 8.46667cm x 5.64444cm
breadboards: 1

parts:
  Teensy_3_1 = Teensy 3.1
  LED1 = smd LED [color="Red (633nm)" package="1206 [SMD]"]
  R1 = Resistor [tolerance=±5% resistance=470 package="2512 [SMD]"]

nets:
  N1: Teensy_3_1.GND, R1.Pin_1
  N2: Teensy_3_1.A9/D23, LED1.anode
  N3: LED1.cathode, R1.Pin_0
