# Fritzing sketch L03_ButtonLED (saved by Fritzing 0.9.3b)
circuit board: 8.46667cm x 5.64444cm
breadboards: 1

parts:
  Teensy_3_1 = Teensy 3.1
  R4 = Resistor [tolerance=±5% resistance=220 package="0603 [SMD]"]
  LED1 = smd LED [color="Red (633nm)" package="1206 [SMD]"]
  R5 = Resistor [tolerance=±5% resistance=220 package="0603 [SMD]"]
  S2 = Pushbutton [package="[THT]"]
  S3 = Pushbutton [package="[THT]"]
  S5 = Pushbutton [package="[THT]"]
  R6 = Resistor [tolerance=±5% resistance=220 package="0603 [SMD]"]

nets:
  N1: Teensy_3_1.GND, R4.Pin_1, R5.Pin_1, S5.Pin_3, S5.Pin_4
  N2: Teensy_3_1.D5, LED1.anode
  N3: Teensy_3_1.A1/D15, S3.Pin_1, S3.Pin_2
  N4: Teensy_3_1.A2/D16, S5.Pin_1, S5.Pin_2, R6.Pin_1
  N5: Teensy_3_1.A9/D23, R5.Pin_0, S2.Pin_1, S2.Pin_2
  N6: Teensy_3_1.3V3, S2.Pin_3, S2.Pin_4, R6.Pin_0
  N7: R4.Pin_0, LED1.cathode
  N8: S3.Pin_3, S3.Pin_4

notes:
  The blue button is wired with a pull down resistor.
  The green button with a pull up resistor.
  The red button has no external pull down/up, but instead uses pinMode(pin,INPUT_PULLUP).

custom parts:
  Pushbutton: A generic pushbutton.
  Pushbutton: A generic pushbutton.
  Pushbutton: A generic pushbutton.

// code stored in the sketch: 05_oneButtonArray.ino
/*
 * Project: Using OneButton library
 * Description: Introduct Students to OneButton Library using 2 buttons
 * Author: Brian A Rashap
 * Date: 13-Dec-2019
 */

#include "OneButton.h"

// Setup OneButton on pin 18 and pin 17
OneButton button1(18, false); 
OneButton button2(17, false);

// LED pin configure
int ledPin = 23;
int ledPin2 = 5;
int ledPin3 = 4;
int ledDelay = 50;

int ledArray[] = {ledPin, ledPin2, ledPin3};

boolean buttonState = LOW;
boolean buttonState2 = LOW;
boolean flash = LOW;

int n;
int j = 0;

void setup() {

  Serial.begin(9600);
  while (!Serial); 

  pinMode(ledPin, OUTPUT);
  pinMode(ledPin2, OUTPUT);
  pinMode(ledPin3, OUTPUT);

  for (n = 0; n<3; n++) {
    Serial.print(ledArray[n]);
    Serial.print(" , ");
  }
  Serial.println();

  // link the button 1 functions.
  button1.attachClick(click1);
  button1.attachDoubleClick(doubleclick1);
  button1.attachLongPressStart(longPressStart1);
  button1.attachLongPressStop(longPressStop1);
  //button1.attachDuringLongPress(longPress1);
  button1.setClickTicks(250);
  button1.setPressTicks(2000);

  // link the button 2 functions.
  button2.attachClick(click2);
  button2.attachDoubleClick(doubleclick2);
  button2.attachLongPressStart(longPressStart2);
  button2.attachLongPressStop(longPressStop2);
  //button2.attachDuringLongPress(longPress2);
  button2.setClickTicks(250);
  button2.setPressTicks(1000);

  if(Serial) Serial.println("Starting TwoButtons...");

} 

void loop() {
  // keep watching the push buttons:
  button1.tick();
  button2.tick();
}


// ----- button 1 callback functions

// This function will be called when the button1 was pressed 1 time (and no 2. button press followed).
void click1() {
  Serial.println("Button 1 click.");
  buttonState = !buttonState;
  Serial.print("buttonState = ");
  Serial.println(buttonState);
  if (buttonState == LOW) digitalWrite(ledArray[j], LOW);
  else digitalWrite(ledArray[j], HIGH);
  
} // click1


// This function will be called when the button1 was pressed 2 times in a short timeframe.
void doubleclick1() {
  Serial.println("Button 1 doubleclick.");
  j++;
  if (j > 2) j = 0;
  Serial.print("j = ");
  Serial.println(j);
} // doubleclick1


// This function will be called once, when the button1 is pressed for a long time.
void longPressStart1() {
  Serial.println("Button 1 longPress start");
} // longPressStart1


// This function will be called often, while the button1 is pressed for a long time.
void longPress1() {
  Serial.println("Button 1 longPress...");
} // longPress1


// This function will be called once, when the button1 is released after beeing pressed for a long time.
void longPressStop1() {
  Serial.println("Button 1 longPress stop");
} // longPressStop1


// ... and the same for button 2:

void click2() {
  Serial.println("Button 2 click.");
} // click2


void doubleclick2() {
  Serial.println("Button 2 doubleclick.");
} // doubleclick2


void longPressStart2() {
  Serial.println("Button 2 longPress start");
} // longPressStart2


void longPress2() {
  Serial.println("Button 2 longPress...");
} // longPress2

void longPressStop2() {
  Serial.println("Button 2 longPress stop");
} // longPressStop2
