# Fritzing sketch L06_Encoder (saved by Fritzing 0.9.9b)
breadboards: 3

parts:
  Breadboard4 = Breadboard Split Power
  Breadboard5 = Breadboard Split Power
  Neopixel1 = Adafruit RBG Smart Neopixel [package="DIP (Dual Inline) [THT]"]
  Teensy_3_1 = Teensy 3.1
  Neopixel2 = Adafruit RBG Smart Neopixel [package="DIP (Dual Inline) [THT]"]
  Neopixel3 = Adafruit RBG Smart Neopixel [package="DIP (Dual Inline) [THT]"]
  Part1 = 12 NeoPixel Ring [part_number=1643]
  RG_encoder2 = SprkFn RG Encoder [package="DIP (Dual Inline) [THT]"]
  C1 = Capacitor [part_number=475 package=cap-pth-small2]
  R1 = Resistor [tolerance=±1% resistance=470 package="2010 [SMD]"]
  R2 = Trimmer Potentiometer [maximum_resistance=10kΩ package=THT]
  Neopixel5 = Adafruit RBG Smart Neopixel [package="DIP (Dual Inline) [THT]"]
  C2 = Capacitor [package=cap-pth-small2]
  C3 = Capacitor [package=cap-pth-small2]

nets:
  GND: Breadboard4.pin3Z, Breadboard4.pin21Z, Breadboard4.pin29Z, Breadboard5.pin3Z, Breadboard5.pin10Z, Neopixel1.G, Teensy_3_1.GND, Neopixel2.G, Neopixel3.G, Neopixel3.O, Part1.IN, Part1.GND, RG_encoder2.B, C1.1, Neopixel5.G, C2.2, C3.1
  N1: Breadboard4.pin4Y, Breadboard4.pin15Y, Breadboard4.pin17Y, Breadboard4.pin22Y, Breadboard4.pin29Y, Breadboard5.pin3Y, Breadboard5.pin15Y, Breadboard5.pin17Y, Breadboard5.pin29Y, R2.leg2
  N2: Neopixel1.+, Neopixel2.+, Neopixel3.+, Part1.VDD, Neopixel5.+
  N3: Neopixel1.In, Neopixel5.O
  N4: Neopixel1.O, Neopixel2.In
  N5: Teensy_3_1.D1, RG_encoder2.A, C3.2
  N6: Teensy_3_1.D2, RG_encoder2.C, C2.1
  N7: Teensy_3_1.A14/DAC, Teensy_3_1.A0/D14, R1.Pin_0
  N8: Teensy_3_1.A1/D15, C1.2, R1.Pin_1
  N9: Teensy_3_1.A2/D16, R2.wiper
  N10: Teensy_3_1.A3/D17, Neopixel5.In
  N11: Neopixel2.O, Neopixel3.In

custom parts:
  Breadboard Split Power: A custom 6 pin per group power supply strip where the top row (ground) is all bussed together and the bottom row (+V) is split in two groups of 12 pins. This version is modified to be a loadable part and was rescaled to be on the standard 1px = 1thou grid with the size set in inches
  12 NeoPixel Ring: 12 ultra bright smart LED NeoPixels are arranged in a circle with 1.5" (37mm) outer diameter. The rings are 'chainable' - connect the output pin of one to the input pin of another. Use only one microcontroller pin to control as many as you can chain together! Each LED is addressable as the driver chip is inside the LED. Each one has ~18mA constant current drive so the color will be very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
  SprkFn RG Encoder: SparkFun RG Rotary Encoder
