# Fritzing sketch L08_BB (saved by Fritzing 0.9.4)
breadboards: 3

parts:
  Breadboard4 = Breadboard Split Power
  Breadboard5 = Breadboard Split Power
  Teensy_3_1 = Teensy 3.1
  WIZ820io1 = WIZ820io [part_number=WIZ820io]

nets:
  N1: Breadboard4.pin15Y, Breadboard4.pin17Y, Breadboard4.pin29Y, Breadboard5.pin3Y, Breadboard5.pin15Y, Breadboard5.pin17Y
  N2: Breadboard4.pin29Z, Breadboard5.pin3Z
  GND: Teensy_3_1.GND, WIZ820io1.GND
  N3: Teensy_3_1.D9, WIZ820io1.nRESET
  N4: Teensy_3_1.D11, WIZ820io1.MOSI
  N5: Teensy_3_1.D12, WIZ820io1.MISO
  N6: Teensy_3_1.D13, WIZ820io1.SCLK
  3V3: Teensy_3_1.3V3, WIZ820io1.VIN

custom parts:
  Breadboard Split Power: A custom 6 pin per group power supply strip where the top row (ground) is all bussed together and the bottom row (+V) is split in two groups of 12 pins. This version is modified to be a loadable part and was rescaled to be on the standard 1px = 1thou grid with the size set in inches
