# Fritzing sketch L08_Wiznet820io (saved by Fritzing 0.9.4)
circuit board: 8.60778cm x 4.04989cm
breadboards: 1

parts:
  Teensy_3_1 = Teensy 3.1
  WIZ820io1 = WIZ820io [part_number=WIZ820io]

nets:
  GND: Teensy_3_1.GND, WIZ820io1.GND
  N1: Teensy_3_1.D9, WIZ820io1.nRESET
  N2: Teensy_3_1.D10, WIZ820io1.nSS
  N3: Teensy_3_1.D11, WIZ820io1.MOSI
  N4: Teensy_3_1.D12, WIZ820io1.MISO
  N5: Teensy_3_1.D13, WIZ820io1.SCLK
  3V3: Teensy_3_1.3V3, WIZ820io1.VIN

// code stored in the sketch: 20_Wiznet820io.ino
//Dynamic Host Configuration protocol 
//(connect to rj45) (get dhcp address) - spoof mac id
#include <SPI.h>
#include <Ethernet.h>

//Enter a MAC address for your controller
//Newer Ethernet shields have a MAC address printed on a sticker on the back
byte mac[] = {
  0x00, 0xAA, 0xBB, 0xCC, 0xDE,  0xFF };

//intialize Ethernet client library
//with the IP address and port of the server
//that you want to connect to (port 80 is default for http):
EthernetClient client;

void setup() {
  
  pinMode(10, OUTPUT);
  digitalWrite(10, HIGH);

  pinMode(4, OUTPUT);
  digitalWrite(4, HIGH);

  pinMode(23, OUTPUT);
  digitalWrite(23, HIGH);

  //Open Serial Communication and wait for port to open:
  Serial.begin(9600);
  while (!Serial) {
    ; //Wait to connect needed for Leonardo only
    }

  pinMode(9, OUTPUT);
  digitalWrite(9, LOW);
  delay(1000);
  digitalWrite(9, HIGH);

  //Start ethernet connection
  if (Ethernet.begin(mac) == 0) {
    Serial.println("failed to configure Ethernet using DHCP");
    //no point in continueing 
    for(;;)
      ;
    
    }
  //print your local IP address
  Serial.print("My IP address:");
  for (byte thisbyte = 0; thisbyte < 4; thisbyte++) {
    //print value of each byte of the IP address
    Serial.print(Ethernet.localIP()[thisbyte], DEC);
    if (thisbyte < 3) Serial.print(".");
    }
  Serial.println();
}

void loop() {
  //empty

}
