# Fritzing sketch L08_Wiznet820io_uSD (saved by Fritzing 0.9.4)
breadboards: 1

parts:
  Part1 = Adafruit MicroSD card breakout board [part_number="Adafruit #254"]
  WIZ820io2 = WIZ820io [part_number=WIZ820io]
  Teensy_3_1 = Teensy 3.1

nets:
  VCC: Part1.VCC, WIZ820io2.VIN
  GND: Part1.GND, WIZ820io2.GND
  N1: Part1.CLK, WIZ820io2.SCLK, Teensy_3_1.D13
  N2: Part1.DO, WIZ820io2.MISO, Teensy_3_1.D12
  N3: Part1.DI, WIZ820io2.MOSI, Teensy_3_1.D11
  N4: Part1.CS, Teensy_3_1.D4
  N5: WIZ820io2.nSS, Teensy_3_1.D10
  N6: WIZ820io2.nRESET, Teensy_3_1.D9

custom parts:
  Adafruit MicroSD card breakout board: Not just a simple breakout board, this microSD adapter goes the extra mile - designed for ease of use. Onboard 5v->3v regulator provides 150mA for power-hungry cards 3v level shifting means you can use this with ease on either 3v or 5v systems Uses a proper level shifting chip, not resistors: less problems, and faster read/write access Use 3 or 4 digital pins to read and write 2Gb+ of storage!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

// code stored in the sketch: 20_Wiznet820io.ino
//Dynamic Host Configuration protocol 
//(connect to rj45) (get dhcp address) - spoof mac id
#include <SPI.h>
#include <Ethernet.h>

//Enter a MAC address for your controller
//Newer Ethernet shields have a MAC address printed on a sticker on the back
byte mac[] = {
  0x00, 0xAA, 0xBB, 0xCC, 0xDE,  0xFF };

//intialize Ethernet client library
//with the IP address and port of the server
//that you want to connect to (port 80 is default for http):
EthernetClient client;

void setup() {
  
  pinMode(10, OUTPUT);
  digitalWrite(10, HIGH);

  pinMode(4, OUTPUT);
  digitalWrite(4, HIGH);

  pinMode(23, OUTPUT);
  digitalWrite(23, HIGH);

  //Open Serial Communication and wait for port to open:
  Serial.begin(9600);
  while (!Serial) {
    ; //Wait to connect needed for Leonardo only
    }

  pinMode(9, OUTPUT);
  digitalWrite(9, LOW);
  delay(1000);
  digitalWrite(9, HIGH);

  //Start ethernet connection
  if (Ethernet.begin(mac) == 0) {
    Serial.println("failed to configure Ethernet using DHCP");
    //no point in continueing 
    for(;;)
      ;
    
    }
  //print your local IP address
  Serial.print("My IP address:");
  for (byte thisbyte = 0; thisbyte < 4; thisbyte++) {
    //print value of each byte of the IP address
    Serial.print(Ethernet.localIP()[thisbyte], DEC);
    if (thisbyte < 3) Serial.print(".");
    }
  Serial.println();
}

void loop() {
  //empty

}
