# Fritzing sketch L10_I2C (saved by Fritzing 0.9.4)
breadboards: 1

parts:
  Teensy_3_1 = Teensy 3.1
  OLED_I2C1 = OLED 128x64 I2C Monochrome Display
  M1 = BMP280

nets:
  GND: Teensy_3_1.GND, OLED_I2C1.GND, M1.GND
  N1: Teensy_3_1.A4/D18, OLED_I2C1.SDA, M1.SDA
  N2: Teensy_3_1.A5/D19, OLED_I2C1.SCK, M1.SCL
  3V3: Teensy_3_1.3V3, OLED_I2C1.VDD, M1.VIN

custom parts:
  BMP280: Temperature Humidity Barometric presure Sensor, I2C
