# Fritzing sketch L10_I2C_Devices (saved by Fritzing 0.9.9b)
breadboards: 3

parts:
  Breadboard4 = Breadboard Split Power
  Breadboard5 = Breadboard Split Power
  Neopixel1 = Adafruit RBG Smart Neopixel [package="DIP (Dual Inline) [THT]"]
  Teensy_3_1 = Teensy 3.1
  Neopixel2 = Adafruit RBG Smart Neopixel [package="DIP (Dual Inline) [THT]"]
  Neopixel3 = Adafruit RBG Smart Neopixel [package="DIP (Dual Inline) [THT]"]
  Part1 = 12 NeoPixel Ring [part_number=1643]
  RG_encoder2 = SprkFn RG Encoder [package="DIP (Dual Inline) [THT]"]
  Neopixel5 = Adafruit RBG Smart Neopixel [package="DIP (Dual Inline) [THT]"]
  C2 = Capacitor [package=cap-pth-small2]
  C3 = Capacitor [package=cap-pth-small2]
  OLED_I2C1 = OLED 128x64 I2C Monochrome Display
  M1 = BMP280

nets:
  GND: Breadboard4.pin3Z, Breadboard4.pin21Z, Breadboard4.pin29Z, Breadboard5.pin3Z, Breadboard5.pin10Z, Neopixel1.G, Teensy_3_1.GND, Neopixel2.G, Neopixel3.G, Neopixel3.O, Part1.IN, Part1.GND, RG_encoder2.B, Neopixel5.G, C2.2, C3.1, OLED_I2C1.GND, M1.GND
  VDD: Breadboard4.pin4Y, Breadboard4.pin15Y, Breadboard4.pin17Y, Breadboard4.pin22Y, Breadboard4.pin29Y, Breadboard5.pin3Y, Breadboard5.pin15Y, Breadboard5.pin17Y, Breadboard5.pin29Y, OLED_I2C1.VDD, M1.VIN
  N1: Neopixel1.+, Neopixel2.+, Neopixel3.+, Part1.VDD, Neopixel5.+
  N2: Neopixel1.In, Neopixel5.O
  N3: Neopixel1.O, Neopixel2.In
  N4: Teensy_3_1.D1, RG_encoder2.A, C3.2
  N5: Teensy_3_1.D2, RG_encoder2.C, C2.1
  N6: Teensy_3_1.A3/D17, Neopixel5.In
  N7: Teensy_3_1.A4/D18, OLED_I2C1.SDA, M1.SDA
  N8: Teensy_3_1.A5/D19, OLED_I2C1.SCK, M1.SCL
  N9: Neopixel2.O, Neopixel3.In

custom parts:
  Breadboard Split Power: A custom 6 pin per group power supply strip where the top row (ground) is all bussed together and the bottom row (+V) is split in two groups of 12 pins. This version is modified to be a loadable part and was rescaled to be on the standard 1px = 1thou grid with the size set in inches
  12 NeoPixel Ring: 12 ultra bright smart LED NeoPixels are arranged in a circle with 1.5" (37mm) outer diameter. The rings are 'chainable' - connect the output pin of one to the input pin of another. Use only one microcontroller pin to control as many as you can chain together! Each LED is addressable as the driver chip is inside the LED. Each one has ~18mA constant current drive so the color will be very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
  SprkFn RG Encoder: SparkFun RG Rotary Encoder
  BMP280: Temperature Humidity Barometric presure Sensor, I2C
