# Fritzing sketch L11_Hue (saved by Fritzing 0.9.4)
breadboards: 1

parts:
  WIZ820io2 = WIZ820io [part_number=WIZ820io]
  Teensy_3_1 = Teensy 3.1
  S1 = Pushbutton [package="[THT]"]
  R1 = Resistor [tolerance=±5% resistance=220 package="2010 [SMD]"]

nets:
  N1: WIZ820io2.GND, R1.Pin_1
  N2: WIZ820io2.MOSI, Teensy_3_1.D11
  N3: WIZ820io2.SCLK, Teensy_3_1.D13
  N4: WIZ820io2.nSS, Teensy_3_1.D10
  N5: WIZ820io2.MISO, Teensy_3_1.D12
  N6: WIZ820io2.nRESET, Teensy_3_1.D9
  N7: WIZ820io2.VIN, S1.Pin_3, S1.Pin_4
  N8: S1.Pin_1, S1.Pin_2, R1.Pin_0

custom parts:
  Pushbutton: A generic pushbutton.

// code stored in the sketch: 20_Wiznet820io.ino
//Dynamic Host Configuration protocol 
//(connect to rj45) (get dhcp address) - spoof mac id
#include <SPI.h>
#include <Ethernet.h>

//Enter a MAC address for your controller
//Newer Ethernet shields have a MAC address printed on a sticker on the back
byte mac[] = {
  0x00, 0xAA, 0xBB, 0xCC, 0xDE,  0xFF };

//intialize Ethernet client library
//with the IP address and port of the server
//that you want to connect to (port 80 is default for http):
EthernetClient client;

void setup() {
  
  pinMode(10, OUTPUT);
  digitalWrite(10, HIGH);

  pinMode(4, OUTPUT);
  digitalWrite(4, HIGH);

  pinMode(23, OUTPUT);
  digitalWrite(23, HIGH);

  //Open Serial Communication and wait for port to open:
  Serial.begin(9600);
  while (!Serial) {
    ; //Wait to connect needed for Leonardo only
    }

  pinMode(9, OUTPUT);
  digitalWrite(9, LOW);
  delay(1000);
  digitalWrite(9, HIGH);

  //Start ethernet connection
  if (Ethernet.begin(mac) == 0) {
    Serial.println("failed to configure Ethernet using DHCP");
    //no point in continueing 
    for(;;)
      ;
    
    }
  //print your local IP address
  Serial.print("My IP address:");
  for (byte thisbyte = 0; thisbyte < 4; thisbyte++) {
    //print value of each byte of the IP address
    Serial.print(Ethernet.localIP()[thisbyte], DEC);
    if (thisbyte < 3) Serial.print(".");
    }
  Serial.println();
}

void loop() {
  //empty

}
