# Fritzing sketch L12_HelloParticle (saved by Fritzing 0.9.4)
breadboards: 1

parts:
  Argon1 = Particle Argon
  P1 = S1133 Si Photodiode [package="8mm Ceramic [THT]"]
  LED1 = smd LED [color="Blue (430nm)" package="0603 [SMD]"]
  R1 = Resistor [tolerance=±5% resistance=220 package="0805 [SMD]"]
  R2 = Resistor [tolerance=±5% resistance=220 package="0805 [SMD]"]

nets:
  N1: Argon1.3.3V, P1.cathode
  N2: Argon1.GND, R1.Pin_1, R2.Pin_1
  N3: Argon1.A0, P1.anode, R2.Pin_0
  N4: Argon1.D4, LED1.anode
  N5: LED1.cathode, R1.Pin_0

custom parts:
  Particle Argon: The Argon is a powerful Wi-Fi enabled development board that can act as either a standalone Wi-Fi endpoint or Wi-Fi enabled gateway for Particle Mesh networks. It is based on the Nordic nRF52840 and has built-in battery charging circuitry so it’s easy to connect a Li-Po and deploy your local network in minutes. The Argon is great for connecting existing projects to the Particle Device Cloud or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
