# Fritzing sketch L13_00_DAC (saved by Fritzing 0.9.4)
breadboards: 1

parts:
  Argon1 = Particle Argon
  C1 = Capacitor [package=cap-pth-small2]
  C2 = Capacitor [package=cap-pth-small2]
  R1 = Resistor [tolerance=±5% resistance=220 package="0402 [SMD]"]
  R2 = Resistor [tolerance=±5% resistance=470 package="0402 [SMD]"]
  J1 = Camdenboss CTB0158-2 [part_number=CTB0158-2 package=THT]

nets:
  N1: Argon1.GND, C2.2
  N2: Argon1.A0, R1.Pin_0
  N3: C1.1, R1.Pin_1, R2.Pin_0
  N4: C2.1, R2.Pin_1, J1.pin2

custom parts:
  Particle Argon: The Argon is a powerful Wi-Fi enabled development board that can act as either a standalone Wi-Fi endpoint or Wi-Fi enabled gateway for Particle Mesh networks. It is based on the Nordic nRF52840 and has built-in battery charging circuitry so it’s easy to connect a Li-Po and deploy your local network in minutes. The Argon is great for connecting existing projects to the Particle Device Cloud or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
