# Fritzing sketch L13_01_NeoPixel (saved by Fritzing 0.9.4)
breadboards: 1

parts:
  Argon1 = Particle Argon
  C1 = Capacitor [package=cap-pth-small2]
  C2 = Capacitor [package=cap-pth-small2]
  Neopixel1 = Adafruit RBG Smart Neopixel [package="DIP (Dual Inline) [THT]"]
  R1 = Resistor [tolerance=±5% resistance=220 package="0402 [SMD]"]
  R2 = Resistor [tolerance=±5% resistance=220 package="0402 [SMD]"]
  J1 = Camdenboss CTB0158-2 [part_number=CTB0158-2 package=THT]
  R3 = Resistor [tolerance=±5% resistance=220 package="0402 [SMD]"]
  R4 = Resistor [tolerance=±5% resistance=220 package="0402 [SMD]"]
  Q1 = PNP-Transistor [package="SOT-23 [SMD]"]

nets:
  N1: Argon1.3.3V, Neopixel1.+, R4.Pin_1
  N2: Argon1.GND, C1.2, C2.2, Neopixel1.G, Q1.1
  N3: Argon1.A0, R1.Pin_0
  N4: Argon1.D4, R3.Pin_0
  N5: C1.1, R1.Pin_1, R2.Pin_0
  N6: C2.1, R2.Pin_1, J1.pin2
  N7: Neopixel1.O, R4.Pin_0, Q1.2
  N8: R3.Pin_1, Q1.0

custom parts:
  Particle Argon: The Argon is a powerful Wi-Fi enabled development board that can act as either a standalone Wi-Fi endpoint or Wi-Fi enabled gateway for Particle Mesh networks. It is based on the Nordic nRF52840 and has built-in battery charging circuitry so it’s easy to connect a Li-Po and deploy your local network in minutes. The Argon is great for connecting existing projects to the Particle Device Cloud or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
