# Fritzing sketch L13_02_NPNAmp (saved by Fritzing 0.9.4)
breadboards: 1

parts:
  Argon1 = Particle Argon
  C1 = Capacitor [package=cap-pth-small2]
  C2 = Capacitor [package=cap-pth-small2]
  R1 = Resistor [tolerance=±5% resistance=220 package="0402 [SMD]"]
  R2 = Resistor [tolerance=±5% resistance=470 package="0402 [SMD]"]
  J1 = Camdenboss CTB0158-2 [part_number=CTB0158-2 package=THT]
  C3 = Capacitor [package=cap-pth-small2]
  R3 = Resistor [tolerance=±5% resistance=10k package="0402 [SMD]"]
  R4 = Resistor [tolerance=±5% resistance=1.8k package="0402 [SMD]"]
  R5 = Resistor [tolerance=±5% resistance=180 package="0402 [SMD]"]
  R6 = Resistor [tolerance=±5% resistance=1.2k package="0402 [SMD]"]
  C4 = Capacitor [package=cap-pth-small2]
  J2 = Camdenboss CTB0158-2 [part_number=CTB0158-2 package=THT]
  Q2 = NPN-Transistor [package="TO92 [THT]"]

nets:
  N1: Argon1.GND, C2.2, R4.Pin_1, R5.Pin_1, J2.pin2
  N2: Argon1.A0, R1.Pin_0
  N3: C1.1, R1.Pin_1, R2.Pin_0
  N4: C2.1, R2.Pin_1, C3.1
  N5: J1.pin1, C4.2
  N6: C3.2, R3.Pin_1, R4.Pin_0, Q2.B
  N7: R3.Pin_0, R6.Pin_0, J2.pin1
  N8: R5.Pin_0, Q2.E
  N9: R6.Pin_1, C4.1, Q2.C

custom parts:
  Particle Argon: The Argon is a powerful Wi-Fi enabled development board that can act as either a standalone Wi-Fi endpoint or Wi-Fi enabled gateway for Particle Mesh networks. It is based on the Nordic nRF52840 and has built-in battery charging circuitry so it’s easy to connect a Li-Po and deploy your local network in minutes. The Argon is great for connecting existing projects to the Particle Device Cloud or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
