# Fritzing sketch L13_03_OpAmp (saved by Fritzing 0.9.4)
breadboards: 1

parts:
  Argon1 = Particle Argon
  C1 = Capacitor [package=cap-pth-small2]
  C2 = Capacitor [package=cap-pth-small2]
  R1 = Resistor [tolerance=±5% resistance=220 package="0402 [SMD]"]
  R2 = Resistor [tolerance=±5% resistance=470 package="0402 [SMD]"]
  J1 = Camdenboss CTB0158-2 [part_number=CTB0158-2 package=THT]
  IC1 = DIP - 8 pins [part_number=LM741 package="DIP (Dual Inline) [THT]"]
  R3 = Resistor [tolerance=±5% resistance=220 package="0402 [SMD]"]
  J2 = Camdenboss CTB0158-3 [part_number=CTB0158-3 package=THT]
  R4 = Trimmer Potentiometer [maximum_resistance=10kΩ package=THT]

nets:
  N1: Argon1.GND, C2.2, IC1.pin3, J2.pin2
  N2: Argon1.A0, R1.Pin_0
  N3: C1.1, R1.Pin_1, R2.Pin_0
  N4: C2.1, R2.Pin_1, R3.Pin_0
  N5: J1.pin2, IC1.pin6, R4.wiper
  N6: IC1.pin2, R3.Pin_1, R4.leg1
  N7: IC1.pin4, J2.pin3
  N8: IC1.pin7, J2.pin1

custom parts:
  Particle Argon: The Argon is a powerful Wi-Fi enabled development board that can act as either a standalone Wi-Fi endpoint or Wi-Fi enabled gateway for Particle Mesh networks. It is based on the Nordic nRF52840 and has built-in battery charging circuitry so it’s easy to connect a Li-Po and deploy your local network in minutes. The Argon is great for connecting existing projects to the Particle Device Cloud or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
  DIP - 8 pins: A DIP stand-in part for whatever IC you want. With 8 pins on a 300 mil dual inline package (DIP) footprint.
