# Fritzing sketch L16_Motion (saved by Fritzing 0.9.4)
breadboards: 1

parts:
  Argon1 = Particle Argon
  Part1 = InvenSense MPU6050
  MOTOR1 = 28BYJ-48 Stepper Motor
  X1 = X113647 Stepper Driver Board [part_number=X113647 package=board]
  Piezoelectric_Sensor1 = Piezoelectric Sensor
  J1 = Camdenboss CTB0158-3 [part_number=CTB0158-3 package=THT]
  J2 = Camdenboss CTB0158-2 [part_number=CTB0158-2 package=THT]
  Load_Cell1 = Load Cell - Red/white/black/green
  Part2 = HX711 Weighing Sensor Module
  Part3 = KY-003 Hall Magnetic Sensor Module [package="Breakout board"]

nets:
  VCC: Argon1.3.3V, Part1.VCC, J1.pin3, J2.pin2, Part2.VCC, Part3.Vin
  GND: Argon1.GND, Part1.GND, X1.GND, Piezoelectric_Sensor1.GND, J1.pin1, J2.pin1, Part2.GND, Part3.-
  N1: Argon1.A0, J1.pin2
  N2: Argon1.SDA, Part1.SDA
  N3: Argon1.SCL, Part1.SCL
  N4: Argon1.D2, Part3.S
  N5: Argon1.D5, Part2.DO/RX
  N6: Argon1.D6, Part2.CK/TX
  N7: Argon1.VUSB, X1.+V
  N8: MOTOR1.BLUE, X1.BLUE
  N9: MOTOR1.PINK, X1.PINK
  N10: MOTOR1.RED, X1.YELLOW
  N11: MOTOR1.ORANGE, X1.ORANGE
  N12: MOTOR1.YELLOW, X1.RED
  N13: Piezoelectric_Sensor1.VCC, J2.terminal_2
  N14: Load_Cell1.wire1, Part2.E+
  N15: Load_Cell1.wire2, Part2.E-
  N16: Load_Cell1.wire3, Part2.A+
  N17: Load_Cell1.wire4, Part2.A-

custom parts:
  Particle Argon: The Argon is a powerful Wi-Fi enabled development board that can act as either a standalone Wi-Fi endpoint or Wi-Fi enabled gateway for Particle Mesh networks. It is based on the Nordic nRF52840 and has built-in battery charging circuitry so it’s easy to connect a Li-Po and deploy your local network in minutes. The Argon is great for connecting existing projects to the Particle Device Cloud or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
  28BYJ-48 Stepper Motor: 28BYJ-48 gear-reduction stepper motor (small)
  X113647 Stepper Driver Board: A common stepper motor driver board based on ULN2003APG darlington array
  Piezoelectric Sensor: Piezoelectric sensor.
  Load Cell - Red/white/black/green: A rectangle load cell/weighting pressure Sensor with four wires - Red, white, black, green. Normally corresponding with E+, E-, A+, A- respectively.
  KY-003 Hall Magnetic Sensor Module: KEYES KY-003 Arduino Hall Magnetic Sensor Module is a switch that will turn on/off in the presence of a magnetic field.
